# Fritzing sketch prototipe-jemuran-arduino (saved by Fritzing 0.9.3b)
breadboards: 1

parts:
  Part1 = Arduino Uno (Rev3) - ICSP
  SERVO1 = Tower Pro SG90 servo [part_number=101246]
  YL-83_-_Detection_Board1 = YL-83 Rain Sensor - Detection Board
  YL-83_-_Control_Board1 = YL-83 Rain Sensor - Control Board

nets:
  N1: Part1.A0, YL-83_-_Control_Board1.AO
  N2: Part1.D9_PWM, SERVO1.Signal
  5V: Part1.5V, SERVO1.+5V, YL-83_-_Control_Board1.VCC
  GND: Part1.GND, SERVO1.GND, YL-83_-_Control_Board1.GND
  N3: YL-83_-_Detection_Board1.POS, YL-83_-_Control_Board1.POS
  N4: YL-83_-_Detection_Board1.NEG, YL-83_-_Control_Board1.NEG

custom parts:
  Tower Pro SG90 servo: Original file by John De Cristofaro http://www.adafruit.com/products/1449 Adafruit Feedback Servo (Small) Edited by: e-radionica.com 28/9/2015
  YL-83 Rain Sensor - Detection Board: The YL-83 is a rain sensor that has more resistance when dry and less resistance when wet. The module runs at 5V.
  YL-83 Rain Sensor - Control Board: The YL-83 is a rain sensor that has more resistance when dry and less resistance when wet. The module runs at 5V.
